// Logisim project Circuit_Design.circ as structural Verilog: 4 circuits, main circuit main
module main (
);

  wire a0, a1, a2, a3, a4, a5, a6, a7, b0, b1, b2, b3, b4, b5, b6, b7, c0, c1, c2, c3, c4, c5, c6, c7,
       clock_1_out, d0, d1, d2, d3, d4, d5, d6, d7, e0, e1, e2, e3, e4, e5, e6, e7, f0, f1, f2, f3, f4, f5,
       f6, f7, g0, g1, g2, g3, g4, g5, g6, g7, h0, h1, h2, h3, h4, h5, h6, h7, n74193_1_q3, n74193_2__co,
       n74193_3__co, n74193_4__co, n74193_5_q3, n74574_1_q0, n74574_1_q1, n74574_1_q2, n74574_1_q3,
       n74574_1_q4, n74574_1_q5, n74574_1_q6, n74574_1_q7, n74574_2_q0, n74574_2_q1, n74574_2_q2,
       n74574_2_q3, n74574_2_q4, n74574_2_q5, n74574_2_q6, n74574_2_q7, n74574_4_q0, n74574_4_q1,
       n74574_4_q2, n74574_4_q3, n74574_4_q4, n74574_4_q5, n74574_4_q6, n74574_4_q7, n74574_6_q0,
       n74574_6_q1, n74574_6_q2, n74574_6_q3, n74574_6_q4, n74574_6_q5, n74574_6_q6, n74574_6_q7,
       n74574_8_q0, n74574_8_q1, n74574_8_q2, n74574_8_q3, n74574_8_q4, n74574_8_q5, n74574_8_q6,
       n74574_8_q7, n74574_10_q0, n74574_10_q1, n74574_10_q2, n74574_10_q3, n74574_10_q4, n74574_10_q5,
       n74574_10_q6, n74574_10_q7, n74574_12_q0, n74574_12_q1, n74574_12_q2, n74574_12_q3, n74574_12_q4,
       n74574_12_q5, n74574_12_q6, n74574_12_q7, n74574_14_q0, n74574_14_q1, n74574_14_q2, n74574_14_q3,
       n74574_14_q4, n74574_14_q5, n74574_14_q6, n74574_14_q7;
  wire [7:0] rom_1_data;
  wire [14:0] n74193_2_q0;

  ROM #(.addrWidth(15)) rom_1 (.addr(n74193_2_q0), .data(rom_1_data));
  Clock clock_1 (.out(clock_1_out));
  _74574 u_74574_1 (
    .Q0(n74574_1_q0), .Q1(n74574_1_q1), .Q2(n74574_1_q2), .Q3(n74574_1_q3), .Q4(n74574_1_q4),
    .Q5(n74574_1_q5), .Q6(n74574_1_q6), .Q7(n74574_1_q7), ._OE(1'b0), .CP(clock_1_out), .D0(rom_1_data[0]),
    .D1(rom_1_data[1]), .D2(rom_1_data[2]), .D3(rom_1_data[3]), .D4(rom_1_data[4]), .D5(rom_1_data[5]),
    .D6(rom_1_data[6]), .D7(rom_1_data[7]), .GND(1'b0), .VCC(1'b1));
  _74193 u_74193_1 (
    .Q3(n74193_1_q3), .VCC(1'b1), ._LD(1'b1), .UP(clock_1_out), .DN(1'b1), .CLR(n74193_1_q3), .GND(1'b0));  // open: _CO, _BO, Q0, Q1, Q2, D3, D0, D1, D2
  _74193 u_74193_2 (
    .Q3(n74193_2_q0[3]), ._CO(n74193_2__co), .Q0(n74193_2_q0[0]), .Q1(n74193_2_q0[1]), .Q2(n74193_2_q0[2]),
    .D3(1'b0), .VCC(1'b1), ._LD(1'b1), .UP(clock_1_out), .DN(1'b1), .CLR(n74193_5_q3), .GND(1'b0), .D0(1'b0),
    .D1(1'b0), .D2(1'b0));  // open: _BO
  _74574 u_74574_2 (
    .Q0(n74574_2_q0), .Q1(n74574_2_q1), .Q2(n74574_2_q2), .Q3(n74574_2_q3), .Q4(n74574_2_q4),
    .Q5(n74574_2_q5), .Q6(n74574_2_q6), .Q7(n74574_2_q7), ._OE(1'b0), .CP(clock_1_out), .D0(n74574_1_q0),
    .D1(n74574_1_q1), .D2(n74574_1_q2), .D3(n74574_1_q3), .D4(n74574_1_q4), .D5(n74574_1_q5),
    .D6(n74574_1_q6), .D7(n74574_1_q7), .GND(1'b0), .VCC(1'b1));
  _74574 u_74574_3 (
    .Q0(h7), .Q1(g7), .Q2(f7), .Q3(e7), .Q4(d7), .Q5(c7), .Q6(b7), .Q7(a7), ._OE(1'b0), .CP(n74193_1_q3),
    .D0(n74574_1_q0), .D1(n74574_1_q1), .D2(n74574_1_q2), .D3(n74574_1_q3), .D4(n74574_1_q4),
    .D5(n74574_1_q5), .D6(n74574_1_q6), .D7(n74574_1_q7), .GND(1'b0));  // open: VCC
  _74193 u_74193_3 (
    .Q3(n74193_2_q0[7]), ._CO(n74193_3__co), .Q0(n74193_2_q0[4]), .Q1(n74193_2_q0[5]), .Q2(n74193_2_q0[6]),
    .D3(1'b0), .VCC(1'b1), ._LD(1'b1), .UP(n74193_2__co), .DN(1'b1), .CLR(n74193_5_q3), .GND(1'b0),
    .D0(1'b0), .D1(1'b0), .D2(1'b0));  // open: _BO
  _74574 u_74574_4 (
    .Q0(n74574_4_q0), .Q1(n74574_4_q1), .Q2(n74574_4_q2), .Q3(n74574_4_q3), .Q4(n74574_4_q4),
    .Q5(n74574_4_q5), .Q6(n74574_4_q6), .Q7(n74574_4_q7), ._OE(1'b0), .CP(clock_1_out), .D0(n74574_2_q0),
    .D1(n74574_2_q1), .D2(n74574_2_q2), .D3(n74574_2_q3), .D4(n74574_2_q4), .D5(n74574_2_q5),
    .D6(n74574_2_q6), .D7(n74574_2_q7), .GND(1'b0), .VCC(1'b1));
  _74574 u_74574_5 (
    .Q0(h6), .Q1(g6), .Q2(f6), .Q3(e6), .Q4(d6), .Q5(c6), .Q6(b6), .Q7(a6), ._OE(1'b0), .CP(n74193_1_q3),
    .D0(n74574_2_q0), .D1(n74574_2_q1), .D2(n74574_2_q2), .D3(n74574_2_q3), .D4(n74574_2_q4),
    .D5(n74574_2_q5), .D6(n74574_2_q6), .D7(n74574_2_q7), .GND(1'b0), .VCC(1'b1));
  _74193 u_74193_4 (
    .Q3(n74193_2_q0[11]), ._CO(n74193_4__co), .Q0(n74193_2_q0[8]), .Q1(n74193_2_q0[9]), .Q2(n74193_2_q0[10]),
    .D3(1'b0), .VCC(1'b1), ._LD(1'b1), .UP(n74193_3__co), .DN(1'b1), .CLR(n74193_5_q3), .GND(1'b0),
    .D0(1'b0), .D1(1'b0), .D2(1'b0));  // open: _BO
  _74193 u_74193_5 (
    .Q3(n74193_5_q3), .Q0(n74193_2_q0[12]), .Q1(n74193_2_q0[13]), .Q2(n74193_2_q0[14]), .D3(1'b0),
    .VCC(1'b1), ._LD(1'b1), .UP(n74193_4__co), .DN(1'b1), .CLR(n74193_5_q3), .GND(1'b0), .D0(1'b0),
    .D1(1'b0), .D2(1'b0));  // open: _CO, _BO
  _74574 u_74574_6 (
    .Q0(n74574_6_q0), .Q1(n74574_6_q1), .Q2(n74574_6_q2), .Q3(n74574_6_q3), .Q4(n74574_6_q4),
    .Q5(n74574_6_q5), .Q6(n74574_6_q6), .Q7(n74574_6_q7), ._OE(1'b0), .CP(clock_1_out), .D0(n74574_4_q0),
    .D1(n74574_4_q1), .D2(n74574_4_q2), .D3(n74574_4_q3), .D4(n74574_4_q4), .D5(n74574_4_q5),
    .D6(n74574_4_q6), .D7(n74574_4_q7), .GND(1'b0), .VCC(1'b1));
  _74574 u_74574_7 (
    .Q0(h5), .Q1(g5), .Q2(f5), .Q3(e5), .Q4(d5), .Q5(c5), .Q6(b5), .Q7(a5), ._OE(1'b0), .CP(n74193_1_q3),
    .D0(n74574_4_q0), .D1(n74574_4_q1), .D2(n74574_4_q2), .D3(n74574_4_q3), .D4(n74574_4_q4),
    .D5(n74574_4_q5), .D6(n74574_4_q6), .D7(n74574_4_q7), .GND(1'b0), .VCC(1'b1));
  _74574 u_74574_8 (
    .Q0(n74574_8_q0), .Q1(n74574_8_q1), .Q2(n74574_8_q2), .Q3(n74574_8_q3), .Q4(n74574_8_q4),
    .Q5(n74574_8_q5), .Q6(n74574_8_q6), .Q7(n74574_8_q7), ._OE(1'b0), .CP(clock_1_out), .D0(n74574_6_q0),
    .D1(n74574_6_q1), .D2(n74574_6_q2), .D3(n74574_6_q3), .D4(n74574_6_q4), .D5(n74574_6_q5),
    .D6(n74574_6_q6), .D7(n74574_6_q7), .GND(1'b0), .VCC(1'b1));
  _74574 u_74574_9 (
    .Q0(h4), .Q1(g4), .Q2(f4), .Q3(e4), .Q4(d4), .Q5(c4), .Q6(b4), .Q7(a4), ._OE(1'b0), .CP(n74193_1_q3),
    .D0(n74574_6_q0), .D1(n74574_6_q1), .D2(n74574_6_q2), .D3(n74574_6_q3), .D4(n74574_6_q4),
    .D5(n74574_6_q5), .D6(n74574_6_q6), .D7(n74574_6_q7), .GND(1'b0), .VCC(1'b1));
  _74574 u_74574_10 (
    .Q0(n74574_10_q0), .Q1(n74574_10_q1), .Q2(n74574_10_q2), .Q3(n74574_10_q3), .Q4(n74574_10_q4),
    .Q5(n74574_10_q5), .Q6(n74574_10_q6), .Q7(n74574_10_q7), ._OE(1'b0), .CP(clock_1_out), .D0(n74574_8_q0),
    .D1(n74574_8_q1), .D2(n74574_8_q2), .D3(n74574_8_q3), .D4(n74574_8_q4), .D5(n74574_8_q5),
    .D6(n74574_8_q6), .D7(n74574_8_q7), .GND(1'b0), .VCC(1'b1));
  _74574 u_74574_11 (
    .Q0(h3), .Q1(g3), .Q2(f3), .Q3(e3), .Q4(d3), .Q5(c3), .Q6(b3), .Q7(a3), ._OE(1'b0), .CP(n74193_1_q3),
    .D0(n74574_8_q0), .D1(n74574_8_q1), .D2(n74574_8_q2), .D3(n74574_8_q3), .D4(n74574_8_q4),
    .D5(n74574_8_q5), .D6(n74574_8_q6), .D7(n74574_8_q7), .GND(1'b0), .VCC(1'b1));
  _74574 u_74574_12 (
    .Q0(n74574_12_q0), .Q1(n74574_12_q1), .Q2(n74574_12_q2), .Q3(n74574_12_q3), .Q4(n74574_12_q4),
    .Q5(n74574_12_q5), .Q6(n74574_12_q6), .Q7(n74574_12_q7), ._OE(1'b0), .CP(clock_1_out), .D0(n74574_10_q0),
    .D1(n74574_10_q1), .D2(n74574_10_q2), .D3(n74574_10_q3), .D4(n74574_10_q4), .D5(n74574_10_q5),
    .D6(n74574_10_q6), .D7(n74574_10_q7), .GND(1'b0), .VCC(1'b1));
  _74574 u_74574_13 (
    .Q0(h2), .Q1(g2), .Q2(f2), .Q3(e2), .Q4(d2), .Q5(c2), .Q6(b2), .Q7(a2), ._OE(1'b0), .CP(n74193_1_q3),
    .D0(n74574_10_q0), .D1(n74574_10_q1), .D2(n74574_10_q2), .D3(n74574_10_q3), .D4(n74574_10_q4),
    .D5(n74574_10_q5), .D6(n74574_10_q6), .D7(n74574_10_q7), .GND(1'b0), .VCC(1'b1));
  _74574 u_74574_14 (
    .Q0(n74574_14_q0), .Q1(n74574_14_q1), .Q2(n74574_14_q2), .Q3(n74574_14_q3), .Q4(n74574_14_q4),
    .Q5(n74574_14_q5), .Q6(n74574_14_q6), .Q7(n74574_14_q7), ._OE(1'b0), .CP(clock_1_out), .D0(n74574_12_q0),
    .D1(n74574_12_q1), .D2(n74574_12_q2), .D3(n74574_12_q3), .D4(n74574_12_q4), .D5(n74574_12_q5),
    .D6(n74574_12_q6), .D7(n74574_12_q7), .GND(1'b0), .VCC(1'b1));
  _74574 u_74574_15 (
    .Q0(h1), .Q1(g1), .Q2(f1), .Q3(e1), .Q4(d1), .Q5(c1), .Q6(b1), .Q7(a1), ._OE(1'b0), .CP(n74193_1_q3),
    .D0(n74574_12_q0), .D1(n74574_12_q1), .D2(n74574_12_q2), .D3(n74574_12_q3), .D4(n74574_12_q4),
    .D5(n74574_12_q5), .D6(n74574_12_q6), .D7(n74574_12_q7), .GND(1'b0), .VCC(1'b1));
  _74574 u_74574_16 (
    .Q0(h0), .Q1(g0), .Q2(f0), .Q3(e0), .Q4(d0), .Q5(c0), .Q6(b0), .Q7(a0), ._OE(1'b0), .CP(n74193_1_q3),
    .D0(n74574_14_q0), .D1(n74574_14_q1), .D2(n74574_14_q2), .D3(n74574_14_q3), .D4(n74574_14_q4),
    .D5(n74574_14_q5), .D6(n74574_14_q6), .D7(n74574_14_q7), .GND(1'b0), .VCC(1'b1));
  _7_Segment_Display u_7_segment_display_1 (.g(g6), .f(b6), .a(c6), .b(d6), .e(a6), .d(f6), .c(e6), .dp(h6));
  _7_Segment_Display u_7_segment_display_2 (.g(g5), .f(b5), .a(c5), .b(d5), .e(a5), .d(f5), .c(e5), .dp(h5));
  _7_Segment_Display u_7_segment_display_3 (.g(g4), .f(b4), .a(c4), .b(d4), .e(a4), .d(f4), .c(e4), .dp(h4));
  _7_Segment_Display u_7_segment_display_4 (.g(g3), .f(b3), .a(c3), .b(d3), .e(a3), .d(f3), .c(e3), .dp(h3));
  _7_Segment_Display u_7_segment_display_5 (.g(g2), .f(b2), .a(c2), .b(d2), .e(a2), .d(f2), .c(e2), .dp(h2));
  _7_Segment_Display u_7_segment_display_6 (.g(g1), .f(b1), .a(c1), .b(d1), .e(a1), .d(f1), .c(e1), .dp(h1));

  // Notes on the sheet:
  //   contents of rom_1 (hex, n*v repeats v):
  //   2 6*0 2 2 2 4*0 2 2 0 2 2 0 2 2 4*0 4*2 4*0 4*2 4*0 4*24 4*0 4*2 4*0 4*24 4*0 4*2 4*0 4*fc 4*0 4*fc
  //   4*0 4*fc 4*0 4*fc 4*0 4*fc 10*0 2 6*0 2 2 2 4*0 2 2 0 2 2 0 2 2 4*0 4*2 4*0 4*2 4*0 4*24 4*0 4*2 4*0
  //   4*24 4*0 4*2 4*0 18 fc fc fc 4*0 18 fc fc fc 4*0 18 fc fc fc 4*0 18 fc fc fc 4*0 18 fc fc fc 10*0 2
  //   6*0 2 2 2 4*0 2 2 0 2 2 0 2 2 4*0 4*2 4*0 4*2 4*0 4*24 4*0 4*2 4*0 4*24 4*0 4*2 4*0 fc 18 fc fc 4*0
  //   fc 18 fc fc 4*0 fc 18 fc fc 4*0 fc 18 fc fc 4*0 fc 18 fc fc 10*0 2 6*0 2 2 2 4*0 2 2 0 2 2 0 2 2 4*0
  //   4*2 4*0 4*2 4*0 4*24 4*0 4*2 4*0 4*24 4*0 4*2 4*0 18 18 fc fc 4*0 18 18 fc fc 4*0 18 18 fc fc 4*0 18
  //   18 fc fc 4*0 18 18 fc fc 10*0 2 6*0 2 2 2 4*0 2 2 0 2 2 0 2 2 4*0 4*2 4*0 4*2 4*0 4*24 4*0 4*2 4*0
  //   4*24 4*0 4*2 4*0 fc fc 18 fc 4*0 fc fc 18 fc 4*0 fc fc 18 fc 4*0 fc fc 18 fc 4*0 fc fc 18 fc 10*0 2
  //   6*0 2 2 2 4*0 2 2 0 2 2 0 2 2 4*0 4*2 4*0 4*2 4*0 4*24 4*0 4*2 4*0 4*24 4*0 4*2 4*0 18 fc 18 fc 4*0
  //   18 fc 18 fc 4*0 18 fc 18 fc 4*0 18 fc 18 fc 4*0 18 fc 18 fc 10*0 2 6*0 2 2 2 4*0 2 2 0 2 2 0 2 2 4*0
  //   4*2 4*0 4*2 4*0 4*24 4*0 4*2 4*0 4*24 4*0 4*2 4*0 fc 18 18 fc 4*0 fc 18 18 fc 4*0 fc 18 18 fc 4*0 fc
  //   18 18 fc 4*0 fc 18 18 fc 10*0 2 6*0 2 2 2 4*0 2 2 0 2 2 0 2 2 4*0 4*2 4*0 4*2 4*0 4*24 4*0 4*2 4*0
  //   4*24 4*0 4*2 4*0 18 18 18 fc 4*0 18 18 18 fc 4*0 18 18 18 fc 4*0 18 18 18 fc 4*0 18 18 18 fc 10*0 2
  //   6*0 2 2 2 4*0 2 2 0 2 2 0 2 2 4*0 4*2 4*0 4*2 4*0 4*24 4*0 4*2 4*0 4*24 4*0 4*2 4*0 fc fc fc 18 4*0
  //   fc fc fc 18 4*0 fc fc fc 18 4*0 fc fc fc 18 4*0 fc fc fc 18 10*0 2 6*0 2 2 2 4*0 2 2 0 2 2 0 2 2 4*0
  //   4*2 4*0 4*2 4*0 4*24 4*0 4*2 4*0 4*24 4*0 4*2 4*0 18 fc fc 18 4*0 18 fc fc 18 4*0 18 fc fc 18 4*0 18
  //   fc fc 18 4*0 18 fc fc 18 10*0 2 6*0 2 2 2 4*0 2 2 0 2 2 0 2 2 4*0 4*2 4*0 4*2 4*0 4*24 4*0 4*2 4*0
  //   4*24 4*0 4*2 4*0 fc 18 fc 18 4*0 fc 18 fc 18 4*0 fc 18 fc 18 4*0 fc 18 fc 18 4*0 fc 18 fc 18 10*0 2
  //   6*0 2 2 2 4*0 2 2 0 2 2 0 2 2 4*0 4*2 4*0 4*2 4*0 4*24 4*0 4*2 4*0 4*24 4*0 4*2 4*0 18 18 fc 18 4*0
  //   18 18 fc 18 4*0 18 18 fc 18 28*0 18 18 fc 18 4*0 18 18 fc 18 4*0 18 18 fc 18 28*0 18 18 fc 18 4*0 18
  //   18 fc 18 4*0 18 18 fc 18 28*0 18 18 fc 18 4*0 18 18 fc 18 4*0 18 18 fc 18 26*0 da 7*0 fa da 6*0 f2
  //   fa da 5*0 f2 f2 fa da 4*0 5a f2 f2 fa da 4*0 5a f2 f2 fa da 0 0 18 0 5a f2 f2 fa da 0 18 18 0 5a f2
  //   f2 fa da c6 18 18 0 5a f2 f2 fa ca c6 18 18 0 5a f2 f2 0 ca c6 18 18 0 5a f2 fa 0 ca c6 18 18 0 5a
  //   8a fa 0 ca c6 18 18 0 8a 8a fa 0 ca c6 18 18 18 8a 8a fa 0 ca c6 18 dc 18 8a 8a fa 0 ca c6 e6 dc 18
  //   8a 8a fa 0 ca 82 e6 dc 18 8a 8a fa 0 6e 82 e6 dc 18 8a 8a fa fa 6e 82 e6 dc 18 8a 8a 82 fa 6e 82 e6
  //   dc 18 8a 5a 82 fa 6e 82 e6 dc 18 0 5a 82 fa 6e 82 e6 dc fa 0 5a 82 fa 6e 82 e6 e6 fa 0 5a 82 fa 6e
  //   82 fe e6 fa 0 5a 82 fa 6e e6 fe e6 fa 0 5a 82 fa e4 e6 fe e6 fa 0 5a 82 e4 e4 e6 fe e6 fa 0 5a fa e4
  //   e4 e6 fe e6 fa 0 fa e4 e4 e6 fe e6 fa 0 fa e4 e4 e6 fe e6 fa 25*0 fa e4 e4 e6 fe e6 fa 0 fa e4 e4 e6
  //   fe e6 fa 0 fa e4 e4 e6 fe e6 fa 25*0 fa e4 e4 e6 fe e6 fa 0 fa e4 e4 e6 fe e6 fa 0 fa e4 e4 e6 fe e6
  //   fa 25*0 fa e4 e4 e6 fe e6 fa 0 fa e4 e4 e6 fe e6 fa 0 fa e4 e4 e6 fe e6 fa 25*0 fa e4 e4 e6 fe e6 fa
  //   0 fa e4 e4 e6 fe e6 fa 0 fa e4 e4 e6 fe e6 fa 28*0 dc c4 5*0 dc fc fc c4 0 0 0 dc fc 5a dc fc c4 0
  //   dc fc 5a 0 e6 dc fc c4 fc 5a 0 0 0 e6 dc fc 5a 5*0 e6 dc 7*0 e6 15*0 e6 5a 5*0 e6 dc fc 5a 0 0 0 e6
  //   dc fc dc fc 5a 0 e6 dc fc c4 0 dc fc 5a dc fc c4 0 0 0 dc fc fc c4 5*0 dc c4 5*0 dc fc fc c4 0 0 0
  //   dc fc 5a dc fc c4 0 dc fc 5a 0 e6 dc fc c4 fc 5a 0 0 0 e6 dc fc 5a 5*0 e6 dc 7*0 e6 15*0 e6 5a 5*0
  //   e6 dc fc 5a 0 0 0 e6 dc fc dc fc 5a 0 e6 dc fc c4 0 dc fc 5a dc fc c4 0 0 0 dc fc fc c4 0 0 0 dc fc
  //   5a dc fc c4 0 dc fc 5a 0 e6 dc fc c4 dc fc 5a 0 e6 dc fc c4 dc fc 5a 0 e6 dc fc c4 24*0 dc fc 5a 0
  //   e6 dc fc c4 dc fc 5a 0 e6 dc fc c4 dc fc 5a 0 e6 dc fc c4 24*0 dc fc 5a 0 e6 dc fc c4 dc fc 5a 0 e6
  //   dc fc c4 dc fc 5a 0 e6 dc fc c4 24*0 dc fc 5a 0 e6 dc fc c4 dc fc 5a 0 e6 dc fc c4 dc fc 5a 0 e6 dc
  //   fc c4 dc fc 5a 0 e6 dc fc c4 dc fc 5a 0 e6 dc fc c4 dc fc 5a 0 e6 dc fc c4 24*0 6e fa fa e6 5a 0 18
  //   18 6e fa fa e6 5a 0 18 18 6e fa fa e6 5a 0 18 18 6e fa fa e6 5a 0 18 18 6e fa fa e6 5a 0 18 18 6e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
endmodule

module _74193 (
  input  VCC,
  input  D0,
  input  D1,
  input  D2,
  input  D3,
  input  _LD,
  input  UP,
  input  DN,
  input  CLR,
  input  GND,
  output _CO,
  output _BO,
  output Q0,
  output Q1,
  output Q2,
  output Q3
);

  wire and_1_out, and_2_out, and_3_out, and_4_out, and_5_out, and_6_out, buffer_1_out, buffer_2_out,
       buffer_3_out, buffer_5_out, buffer_7_out, buffer_9_out, nand_1_out, nand_2_out, nand_3_out,
       nand_4_out, nand_5_out, nand_6_out, nand_7_out, nand_8_out, nand_9_out, nand_10_out, nor_1_out,
       nor_2_out, nor_3_out, nor_4_out, not_1_out, not_2_out, not_3_out, not_4_out, not_5_out, not_6_out,
       not_7_out, not_8_out, or_1_out, or_2_out, or_3_out, or_4_out, t_ff_1_q, t_ff_1_qn, t_ff_2_q,
       t_ff_2_qn, t_ff_3_q, t_ff_3_qn, t_ff_4_q, t_ff_4_qn;

  not not_1 (not_1_out, _LD);
  not not_2 (not_2_out, UP);
  not not_3 (not_3_out, DN);
  not not_4 (not_4_out, CLR);
  buf buffer_1 (buffer_1_out, not_2_out);
  buf buffer_2 (buffer_2_out, not_3_out);
  buf buffer_3 (buffer_3_out, D0);
  nand nand_1 (nand_1_out, not_1_out, buffer_3_out);
  nand nand_2 (nand_2_out, nand_1_out, not_1_out);
  not not_5 (not_5_out, nand_1_out);
  T_Flip_Flop t_ff_1 (
    .clk(nor_1_out), .T(nor_1_out), .Q(t_ff_1_q), .Qn(t_ff_1_qn), .preset(not_5_out), .reset(or_1_out));
  nor nor_1 (nor_1_out, buffer_1_out, buffer_2_out);
  or or_1 (or_1_out, ~not_4_out, ~nand_2_out);  // OR_Gate
  buf buffer_4 (Q0, t_ff_1_q);
  and and_1 (and_1_out, not_2_out, t_ff_1_q);
  and and_2 (and_2_out, t_ff_1_qn, not_3_out);
  nand nand_3 (nand_3_out, not_1_out, buffer_5_out);
  not not_6 (not_6_out, nand_3_out);
  nor nor_2 (nor_2_out, and_1_out, and_2_out);
  buf buffer_5 (buffer_5_out, D1);
  nand nand_4 (nand_4_out, nand_3_out, not_1_out);
  T_Flip_Flop t_ff_2 (
    .clk(nor_2_out), .T(nor_2_out), .Q(t_ff_2_q), .Qn(t_ff_2_qn), .preset(not_6_out), .reset(or_2_out));
  or or_2 (or_2_out, ~not_4_out, ~nand_4_out);  // OR_Gate
  buf buffer_6 (Q1, t_ff_2_q);
  and and_3 (and_3_out, not_2_out, t_ff_1_q, t_ff_2_q);
  and and_4 (and_4_out, t_ff_2_qn, t_ff_1_qn, not_3_out);
  buf buffer_7 (buffer_7_out, D2);
  nand nand_5 (nand_5_out, not_1_out, buffer_7_out);
  not not_7 (not_7_out, nand_5_out);
  nor nor_3 (nor_3_out, and_3_out, and_4_out);
  nand nand_6 (nand_6_out, nand_5_out, not_1_out);
  T_Flip_Flop t_ff_3 (
    .clk(nor_3_out), .T(nor_3_out), .Q(t_ff_3_q), .Qn(t_ff_3_qn), .preset(not_7_out), .reset(or_3_out));
  or or_3 (or_3_out, ~not_4_out, ~nand_6_out);  // OR_Gate
  buf buffer_8 (Q2, t_ff_3_q);
  and and_5 (and_5_out, t_ff_2_q, not_2_out, t_ff_1_q, t_ff_3_q);
  and and_6 (and_6_out, t_ff_3_qn, t_ff_2_qn, t_ff_1_qn, not_3_out);
  nor nor_4 (nor_4_out, and_5_out, and_6_out);
  buf buffer_9 (buffer_9_out, D3);
  nand nand_7 (nand_7_out, not_1_out, buffer_9_out);
  nand nand_8 (nand_8_out, nand_7_out, not_1_out);
  not not_8 (not_8_out, nand_7_out);
  T_Flip_Flop t_ff_4 (
    .clk(nor_4_out), .T(nor_4_out), .Q(t_ff_4_q), .Qn(t_ff_4_qn), .preset(not_8_out), .reset(or_4_out));
  or or_4 (or_4_out, ~not_4_out, ~nand_8_out);  // OR_Gate
  buf buffer_10 (Q3, t_ff_4_q);
  nand nand_9 (nand_9_out, t_ff_3_q, not_2_out, t_ff_4_q, t_ff_2_q, t_ff_1_q);
  buf buffer_11 (_CO, nand_9_out);
  nand nand_10 (nand_10_out, t_ff_1_qn, t_ff_4_qn, t_ff_3_qn, t_ff_2_qn, not_3_out);
  buf buffer_12 (_BO, nand_10_out);
endmodule

module _74574 (
  input  VCC,
  input  _OE,
  input  CP,
  input  D0,
  input  D1,
  input  D2,
  input  D3,
  input  D4,
  input  D5,
  input  D6,
  input  D7,
  input  GND,
  output Q0,
  output Q1,
  output Q2,
  output Q3,
  output Q4,
  output Q5,
  output Q6,
  output Q7
);

  wire d_ff_1_q, d_ff_2_q, d_ff_3_q, d_ff_4_q, d_ff_5_q, d_ff_6_q, d_ff_7_q, d_ff_8_q, not_1_out;

  not not_1 (not_1_out, _OE);
  D_Flip_Flop d_ff_1 (.clk(CP), .D(D0), .Q(d_ff_1_q));  // open: Qn, preset, reset
  D_Flip_Flop d_ff_2 (.clk(CP), .D(D1), .Q(d_ff_2_q));  // open: Qn, preset, reset
  D_Flip_Flop d_ff_3 (.clk(CP), .D(D2), .Q(d_ff_3_q));  // open: Qn, preset, reset
  D_Flip_Flop d_ff_4 (.clk(CP), .D(D3), .Q(d_ff_4_q));  // open: Qn, preset, reset
  D_Flip_Flop d_ff_5 (.clk(CP), .D(D4), .Q(d_ff_5_q));  // open: Qn, preset, reset
  D_Flip_Flop d_ff_6 (.clk(CP), .D(D5), .Q(d_ff_6_q));  // open: Qn, preset, reset
  D_Flip_Flop d_ff_7 (.clk(CP), .D(D6), .Q(d_ff_7_q));  // open: Qn, preset, reset
  D_Flip_Flop d_ff_8 (.clk(CP), .D(D7), .Q(d_ff_8_q));  // open: Qn, preset, reset
  assign Q0 = not_1_out ? d_ff_1_q : 1'bz;  // Controlled_Buffer controlled_buffer_1
  assign Q1 = not_1_out ? d_ff_2_q : 1'bz;  // Controlled_Buffer controlled_buffer_2
  assign Q2 = not_1_out ? d_ff_3_q : 1'bz;  // Controlled_Buffer controlled_buffer_3
  assign Q3 = not_1_out ? d_ff_4_q : 1'bz;  // Controlled_Buffer controlled_buffer_4
  assign Q4 = not_1_out ? d_ff_5_q : 1'bz;  // Controlled_Buffer controlled_buffer_5
  assign Q5 = not_1_out ? d_ff_6_q : 1'bz;  // Controlled_Buffer controlled_buffer_6
  assign Q6 = not_1_out ? d_ff_7_q : 1'bz;  // Controlled_Buffer controlled_buffer_7
  assign Q7 = not_1_out ? d_ff_8_q : 1'bz;  // Controlled_Buffer controlled_buffer_8
endmodule

module _74163 (
  input  _CLR,
  input  VCC,
  input  CP,
  input  D0,
  input  D1,
  input  D2,
  input  D3,
  input  ENP,
  input  ENT,
  input  GND,
  input  _LD,
  output RCO,
  output Q0,
  output Q1,
  output Q2,
  output Q3
);

  wire and_1_out, and_2_out, counter_1_carry, not_1_out, not_2_out;
  wire [3:0] multiplexer_1_out;

  not not_1 (not_1_out, _CLR);
  Multiplexer #(.enable("false"), .width(4)) multiplexer_1 (
    .in0({D3, D2, D1, D0}), .in1(4'b0000), .out(multiplexer_1_out), .sel(not_1_out));
  and and_1 (and_1_out, ENP, and_2_out, ENT);
  Counter #(.max('hf), .width(4)) counter_1 (
    .load(not_2_out), .D(multiplexer_1_out), .count(and_1_out), .Q({Q3, Q2, Q1, Q0}),
    .carry(counter_1_carry), .clk(CP));  // open: clr
  not not_2 (not_2_out, and_2_out);
  and and_2 (and_2_out, ~not_1_out, _LD);  // AND_Gate
  and and_3 (RCO, counter_1_carry, ENT);
endmodule
